# Fritzing sketch weather_demo_nano (saved by Fritzing 0.9.3b)
breadboards: 2

parts:
  LCM1602_IIC2 = LCM1602 IIC [part_number="LCM1602 IIC" chip_label="LCM1602 IIC" package="DIP (Dual Inline) [THT]"]
  R2 = Photocell (LDR) [package=THT]
  Arduino_Nano = Arduino Nano (Rev3.0)
  DHT23 = DHT22 Humidity and Temperature Sensor
  BMP180 = Barometric Pressure Sensor - BMP180 Breakout (GY-68)
  R1 = Resistor [tolerance=±5% resistance=10k package=THT]
  LCD1_20x5 = LCD screen
  R3 = Resistor [tolerance=±5% resistance=10k package=THT]

nets:
  VSS: LCM1602_IIC2.VSS, LCD1_20x5.VSS
  VDD: LCM1602_IIC2.VDD, LCD1_20x5.VDD
  N1: LCM1602_IIC2.V0, LCD1_20x5.V0
  N2: LCM1602_IIC2.RS, LCD1_20x5.RS
  N3: LCM1602_IIC2.RW, LCD1_20x5.R/W
  N4: LCM1602_IIC2.E, LCD1_20x5.E
  N5: LCM1602_IIC2.D0, LCD1_20x5.DB0
  N6: LCM1602_IIC2.D1, LCD1_20x5.DB1
  N7: LCM1602_IIC2.D2, LCD1_20x5.DB2
  N8: LCM1602_IIC2.D3, LCD1_20x5.DB3
  N9: LCM1602_IIC2.D4, LCD1_20x5.DB4
  N10: LCM1602_IIC2.D5, LCD1_20x5.DB5
  N11: LCM1602_IIC2.D6, LCD1_20x5.DB6
  N12: LCM1602_IIC2.D7, LCD1_20x5.DB7
  N13: LCM1602_IIC2.A, LCD1_20x5.LED-
  N14: LCM1602_IIC2.K, LCD1_20x5.LED+
  GND: LCM1602_IIC2.GND, Arduino_Nano.GND, DHT23.GND, BMP180.GND, R3.Pin_0
  VCC: LCM1602_IIC2.VCC, R2.pin_1, Arduino_Nano.5V, DHT23.VDD, BMP180.VCC, R1.Pin_1
  N15: LCM1602_IIC2.SDA, Arduino_Nano.A4, BMP180.SDA
  N16: LCM1602_IIC2.SCL, Arduino_Nano.A5, BMP180.SCL
  N17: LCM1602_IIC2.LED_A, Arduino_Nano.D3
  N18: R2.pin_0, Arduino_Nano.A0, R3.Pin_1
  N19: Arduino_Nano.D7, DHT23.DATA, R1.Pin_0

custom parts:
  LCM1602 IIC: I2C-Module to use a 1602 or 2004 LCD on with the wire.h libory Serial LCD Modul
  LCD screen: A standard character display, usually with 2x16 characters. Comes in many colors.
